// Logisim project CODE.circ as structural Verilog
module XOR (
  input  A,
  input  B,
  output Out
);

  wire nand_1_out, or_1_out;

  or or_1 (or_1_out, A, B);
  nand nand_1 (nand_1_out, A, B);
  and and_1 (Out, or_1_out, nand_1_out);
endmodule

module HalfAdder (
  input  A,
  input  B,
  output Sum,
  output Carry_Out
);

  XOR xor_1 (.A(A), .B(B), .Out(Sum));
  and and_1 (Carry_Out, A, B);
endmodule

module FullAdder (
  input  Clock_In,
  input  A,
  input  B,
  output Sum,
  output Clock_Out
);

  wire halfadder_1_carry_out, halfadder_1_sum, halfadder_2_carry_out;

  HalfAdder halfadder_1 (.A(A), .B(B), .Sum(halfadder_1_sum), .Carry_Out(halfadder_1_carry_out));
  HalfAdder halfadder_2 (.A(Clock_In), .B(halfadder_1_sum), .Sum(Sum), .Carry_Out(halfadder_2_carry_out));
  or or_1 (Clock_Out, halfadder_2_carry_out, halfadder_1_carry_out);
endmodule

module EightBitAdder (
  input  Clock_In,
  input  [7:0] A,
  input  Clock_Out,
  input  [7:0] B,
  output [7:0] Sum
);

  wire fulladder_1_clock_out, fulladder_2_clock_out, fulladder_3_clock_out, fulladder_4_clock_out,
       fulladder_5_clock_out, fulladder_6_clock_out, fulladder_7_clock_out;

  FullAdder fulladder_1 (.A(A[0]), .B(B[0]), .Clock_In(Clock_In), .Clock_Out(fulladder_1_clock_out), .Sum(Sum[0]));
  FullAdder fulladder_2 (
    .A(A[1]), .B(B[1]), .Clock_In(fulladder_1_clock_out), .Clock_Out(fulladder_2_clock_out), .Sum(Sum[1]));
  FullAdder fulladder_3 (
    .A(A[2]), .B(B[2]), .Clock_In(fulladder_2_clock_out), .Clock_Out(fulladder_3_clock_out), .Sum(Sum[2]));
  FullAdder fulladder_4 (
    .A(A[3]), .B(B[3]), .Clock_In(fulladder_3_clock_out), .Clock_Out(fulladder_4_clock_out), .Sum(Sum[3]));
  FullAdder fulladder_5 (
    .A(A[4]), .B(B[4]), .Clock_In(fulladder_4_clock_out), .Clock_Out(fulladder_5_clock_out), .Sum(Sum[4]));
  FullAdder fulladder_6 (
    .A(A[5]), .B(B[5]), .Clock_In(fulladder_5_clock_out), .Clock_Out(fulladder_6_clock_out), .Sum(Sum[5]));
  FullAdder fulladder_7 (
    .A(A[6]), .B(B[6]), .Clock_In(fulladder_6_clock_out), .Clock_Out(fulladder_7_clock_out), .Sum(Sum[6]));
  FullAdder fulladder_8 (.A(A[7]), .B(B[7]), .Clock_In(fulladder_7_clock_out), .Clock_Out(Clock_Out), .Sum(Sum[7]));
endmodule

module OnesCompliment (
  input  Invert,
  input  [7:0] In,
  output [7:0] Out
);

  XOR xor_1 (.A(In[0]), .B(Invert), .Out(Out[0]));
  XOR xor_2 (.A(In[1]), .B(Invert), .Out(Out[1]));
  XOR xor_3 (.A(In[2]), .B(Invert), .Out(Out[2]));
  XOR xor_4 (.A(In[3]), .B(Invert), .Out(Out[3]));
  XOR xor_5 (.A(In[4]), .B(Invert), .Out(Out[4]));
  XOR xor_6 (.A(In[5]), .B(Invert), .Out(Out[5]));
  XOR xor_7 (.A(In[6]), .B(Invert), .Out(Out[6]));
  XOR xor_8 (.A(In[7]), .B(Invert), .Out(Out[7]));
endmodule

module EightBitAdderSubtractor (
  input  Sub,
  input  [7:0] A,
  input  [7:0] B,
  output [7:0] Out,
  output Overflow_Underflow
);

  wire undriven;
  wire [7:0] onescompliment_1_out;

  OnesCompliment onescompliment_1 (.In(A), .Invert(Sub), .Out(onescompliment_1_out));
  EightBitAdder eightbitadder_1 (.A(onescompliment_1_out), .B(B), .Clock_In(Sub), .Clock_Out(undriven), .Sum(Out));
  XOR xor_1 (.A(Sub), .B(undriven), .Out(Overflow_Underflow));
endmodule

module RSFlipFlop (
  input  R,
  input  Enable,
  input  S,
  output Q,
  output QBar
);

  nor nor_1 (Q, R, Enable, QBar);
  nor nor_2 (QBar, Q, Enable, S);
endmodule

module LevelTriggeredDFlipFlop (
  input  Clear,
  input  Clock,
  input  Enable,
  input  Data,
  output Q,
  output QBar,
  output Clear_Out,
  output Clock_Out,
  output Enable_Out
);

  wire and_1_out, and_2_out, not_1_out, or_1_out;

  not not_1 (not_1_out, Data);
  and and_1 (and_1_out, not_1_out, Clock);
  and and_2 (and_2_out, Clock, Data);
  or or_1 (or_1_out, Clear, and_1_out);
  RSFlipFlop rsflipflop_1 (.R(or_1_out), .Enable(Enable), .S(and_2_out), .Q(Q), .QBar(QBar));

  assign Clear_Out = Clear;
  assign Clock_Out = Clock;
  assign Enable_Out = Enable;
endmodule

module EightBitLatch (
  input  Clear,
  input  Clock,
  input  Enable,
  input  [7:0] In,
  output [7:0] Out,
  output Clear_Out,
  output Clock_Out
);

  wire leveltriggereddflipflop_1_clear_out, leveltriggereddflipflop_1_clock_out,
       leveltriggereddflipflop_1_enable_out, leveltriggereddflipflop_2_clear_out,
       leveltriggereddflipflop_2_clock_out, leveltriggereddflipflop_2_enable_out,
       leveltriggereddflipflop_3_clear_out, leveltriggereddflipflop_3_clock_out,
       leveltriggereddflipflop_3_enable_out, leveltriggereddflipflop_4_clear_out,
       leveltriggereddflipflop_4_clock_out, leveltriggereddflipflop_4_enable_out,
       leveltriggereddflipflop_5_clear_out, leveltriggereddflipflop_5_clock_out,
       leveltriggereddflipflop_5_enable_out, leveltriggereddflipflop_6_clear_out,
       leveltriggereddflipflop_6_clock_out, leveltriggereddflipflop_6_enable_out,
       leveltriggereddflipflop_7_clear_out, leveltriggereddflipflop_7_clock_out,
       leveltriggereddflipflop_7_enable_out;

  LevelTriggeredDFlipFlop leveltriggereddflipflop_1 (
    .Data(In[0]), .Clear(Clear), .Clock(Clock), .Enable(Enable),
    .Clear_Out(leveltriggereddflipflop_1_clear_out), .Clock_Out(leveltriggereddflipflop_1_clock_out),
    .Enable_Out(leveltriggereddflipflop_1_enable_out), .Q(Out[0]));  // open: QBar
  LevelTriggeredDFlipFlop leveltriggereddflipflop_2 (
    .Data(In[1]), .Clear(leveltriggereddflipflop_1_clear_out), .Clock(leveltriggereddflipflop_1_clock_out),
    .Enable(leveltriggereddflipflop_1_enable_out), .Clear_Out(leveltriggereddflipflop_2_clear_out),
    .Clock_Out(leveltriggereddflipflop_2_clock_out), .Enable_Out(leveltriggereddflipflop_2_enable_out),
    .Q(Out[1]));  // open: QBar
  LevelTriggeredDFlipFlop leveltriggereddflipflop_3 (
    .Data(In[2]), .Clear(leveltriggereddflipflop_2_clear_out), .Clock(leveltriggereddflipflop_2_clock_out),
    .Enable(leveltriggereddflipflop_2_enable_out), .Clear_Out(leveltriggereddflipflop_3_clear_out),
    .Clock_Out(leveltriggereddflipflop_3_clock_out), .Enable_Out(leveltriggereddflipflop_3_enable_out),
    .Q(Out[2]));  // open: QBar
  LevelTriggeredDFlipFlop leveltriggereddflipflop_4 (
    .Data(In[3]), .Clear(leveltriggereddflipflop_3_clear_out), .Clock(leveltriggereddflipflop_3_clock_out),
    .Enable(leveltriggereddflipflop_3_enable_out), .Clear_Out(leveltriggereddflipflop_4_clear_out),
    .Clock_Out(leveltriggereddflipflop_4_clock_out), .Enable_Out(leveltriggereddflipflop_4_enable_out),
    .Q(Out[3]));  // open: QBar
  LevelTriggeredDFlipFlop leveltriggereddflipflop_5 (
    .Data(In[4]), .Clear(leveltriggereddflipflop_4_clear_out), .Clock(leveltriggereddflipflop_4_clock_out),
    .Enable(leveltriggereddflipflop_4_enable_out), .Clear_Out(leveltriggereddflipflop_5_clear_out),
    .Clock_Out(leveltriggereddflipflop_5_clock_out), .Enable_Out(leveltriggereddflipflop_5_enable_out),
    .Q(Out[4]));  // open: QBar
  LevelTriggeredDFlipFlop leveltriggereddflipflop_6 (
    .Data(In[5]), .Clear(leveltriggereddflipflop_5_clear_out), .Clock(leveltriggereddflipflop_5_clock_out),
    .Enable(leveltriggereddflipflop_5_enable_out), .Clear_Out(leveltriggereddflipflop_6_clear_out),
    .Clock_Out(leveltriggereddflipflop_6_clock_out), .Enable_Out(leveltriggereddflipflop_6_enable_out),
    .Q(Out[5]));  // open: QBar
  LevelTriggeredDFlipFlop leveltriggereddflipflop_7 (
    .Data(In[6]), .Clear(leveltriggereddflipflop_6_clear_out), .Clock(leveltriggereddflipflop_6_clock_out),
    .Enable(leveltriggereddflipflop_6_enable_out), .Clear_Out(leveltriggereddflipflop_7_clear_out),
    .Clock_Out(leveltriggereddflipflop_7_clock_out), .Enable_Out(leveltriggereddflipflop_7_enable_out),
    .Q(Out[6]));  // open: QBar
  LevelTriggeredDFlipFlop leveltriggereddflipflop_8 (
    .Data(In[7]), .Clear(leveltriggereddflipflop_7_clear_out), .Clock(leveltriggereddflipflop_7_clock_out),
    .Enable(leveltriggereddflipflop_7_enable_out), .Clear_Out(Clear_Out), .Clock_Out(Clock_Out), .Q(Out[7]));  // open: Enable_Out, QBar
endmodule

module TwoToOneLineSelector (
  input  Select,
  input  A,
  input  B,
  output out_4,
  output Select_Out
);

  wire and_1_out, and_2_out;

  not not_1 (Select_Out, Select);
  and and_1 (and_1_out, A, Select);
  and and_2 (and_2_out, B, Select_Out);
  or or_1 (out_4, and_1_out, and_2_out);
endmodule

module EightBitTwoOneLineSelector (
  input  Select,
  input  [7:0] A,
  input  [7:0] B,
  output [7:0] Out,
  output Select_Out
);

  wire twotoonelineselector_1_select_out, twotoonelineselector_2_select_out,
       twotoonelineselector_3_select_out, twotoonelineselector_4_select_out,
       twotoonelineselector_5_select_out, twotoonelineselector_6_select_out,
       twotoonelineselector_7_select_out;

  TwoToOneLineSelector twotoonelineselector_1 (
    .A(A[0]), .B(B[0]), .Select(Select), .Select_Out(twotoonelineselector_1_select_out), .out_4(Out[0]));
  TwoToOneLineSelector twotoonelineselector_2 (
    .A(A[1]), .B(B[1]), .Select(twotoonelineselector_1_select_out),
    .Select_Out(twotoonelineselector_2_select_out), .out_4(Out[1]));
  TwoToOneLineSelector twotoonelineselector_3 (
    .A(A[2]), .B(B[2]), .Select(twotoonelineselector_2_select_out),
    .Select_Out(twotoonelineselector_3_select_out), .out_4(Out[2]));
  TwoToOneLineSelector twotoonelineselector_4 (
    .A(A[3]), .B(B[3]), .Select(twotoonelineselector_3_select_out),
    .Select_Out(twotoonelineselector_4_select_out), .out_4(Out[3]));
  TwoToOneLineSelector twotoonelineselector_5 (
    .A(A[4]), .B(B[4]), .Select(twotoonelineselector_4_select_out),
    .Select_Out(twotoonelineselector_5_select_out), .out_4(Out[4]));
  TwoToOneLineSelector twotoonelineselector_6 (
    .A(A[5]), .B(B[5]), .Select(twotoonelineselector_5_select_out),
    .Select_Out(twotoonelineselector_6_select_out), .out_4(Out[5]));
  TwoToOneLineSelector twotoonelineselector_7 (
    .A(A[6]), .B(B[6]), .Select(twotoonelineselector_6_select_out),
    .Select_Out(twotoonelineselector_7_select_out), .out_4(Out[6]));
  TwoToOneLineSelector twotoonelineselector_8 (
    .A(A[7]), .B(B[7]), .Select(twotoonelineselector_7_select_out), .Select_Out(Select_Out), .out_4(Out[7]));
endmodule

module Adder (
  input  Clear,
  input  Clock,
  input  Enable,
  input  Select,
  input  [7:0] A,
  input  [7:0] B,
  output [7:0] Out,
  output Carry_Out
);

  wire [7:0] eightbitlatch_1_out, eightbittwoonelineselector_1_out;

  EightBitLatch eightbitlatch_1 (
    .In(Out), .Clear(Clear), .Clock(Clock), .Enable(Enable), .Out(eightbitlatch_1_out));  // open: Clear_Out, Clock_Out
  EightBitTwoOneLineSelector eightbittwoonelineselector_1 (
    .A(eightbitlatch_1_out), .B(A), .Select(Select), .Out(eightbittwoonelineselector_1_out));  // open: Select_Out
  EightBitAdder eightbitadder_1 (
    .A(eightbittwoonelineselector_1_out), .B(B), .Clock_In(1'b0), .Clock_Out(Carry_Out), .Sum(Out));
endmodule

module EdgeTriggeredDFlipFlop (
  input  Enable,
  input  Data,
  input  Clock,
  output Q,
  output QBar
);

  wire and_1_out, and_2_out, and_3_out, and_4_out, not_1_out, not_2_out, rsflipflop_1_q, rsflipflop_1_qbar;

  not not_1 (not_1_out, Clock);
  not not_2 (not_2_out, Data);
  and and_1 (and_1_out, Data, not_1_out);
  and and_2 (and_2_out, not_1_out, not_2_out);
  RSFlipFlop rsflipflop_1 (.R(and_1_out), .S(and_2_out), .Q(rsflipflop_1_q), .QBar(rsflipflop_1_qbar));  // open: Enable
  and and_3 (and_3_out, rsflipflop_1_q, Clock);
  and and_4 (and_4_out, Clock, rsflipflop_1_qbar);
  RSFlipFlop rsflipflop_2 (.R(and_3_out), .Enable(Enable), .S(and_4_out), .Q(Q), .QBar(QBar));
endmodule
